# Fritzing sketch turnstile (saved by Fritzing 0.9.2b)
breadboards: 1

parts:
  NodeMCU = NodeMCU V1.0
  Lector_RFID = RFID-RC522-v3
  Semáforo_Input = NeoPixel Stick [part_number=1426]
  Semáforo_Output = NeoPixel Stick [part_number=1426]
  LCD1 = LCD screen
  LED1 = LED - 3mm [color="Red (633nm)" package="3 mm [THT]"]
  Input_Sensor = Header 4 [package=jst-4-pth]
  Output_Sensor = Header 4 [package=jst-4-pth]
  LCM1602_IIC2 = LCM1602 IIC [part_number="LCM1602 IIC" chip_label="LCM1602 IIC" package="DIP (Dual Inline) [THT]"]

nets:
  N1: NodeMCU.D0, LED1.anode
  N2: NodeMCU.D1, LCM1602_IIC2.SCL
  N3: NodeMCU.D2, LCM1602_IIC2.SDA
  N4: NodeMCU.D3, Input_Sensor.3
  N5: NodeMCU.D4, Output_Sensor.3
  3V3: NodeMCU.3V3, Lector_RFID.3.3V
  GND: NodeMCU.GND, Lector_RFID.GND, Semáforo_Input.GND, Semáforo_Output.GND, LED1.cathode, Input_Sensor.2, Output_Sensor.2, LCM1602_IIC2.GND
  N6: NodeMCU.D5, Lector_RFID.SCK
  N7: NodeMCU.D6, Lector_RFID.MISO
  N8: NodeMCU.D7, Lector_RFID.MOSI
  N9: NodeMCU.D8, Lector_RFID.SDA
  +5V: NodeMCU.Vin, Semáforo_Input.+5V, Semáforo_Output.+5V, Input_Sensor.1, Output_Sensor.1, LCM1602_IIC2.VCC
  N10: Semáforo_Input.DATAOUT, Semáforo_Output.DATAIN
  VSS: LCD1.VSS, LCM1602_IIC2.VSS
  VDD: LCD1.VDD, LCM1602_IIC2.VDD
  N11: LCD1.V0, LCM1602_IIC2.V0
  N12: LCD1.RS, LCM1602_IIC2.RS
  N13: LCD1.R/W, LCM1602_IIC2.RW
  N14: LCD1.E, LCM1602_IIC2.E
  N15: LCD1.DB0, LCM1602_IIC2.D0
  N16: LCD1.DB1, LCM1602_IIC2.D1
  N17: LCD1.DB2, LCM1602_IIC2.D2
  N18: LCD1.DB3, LCM1602_IIC2.D3
  N19: LCD1.DB4, LCM1602_IIC2.D4
  N20: LCD1.DB5, LCM1602_IIC2.D5
  N21: LCD1.DB6, LCM1602_IIC2.D6
  N22: LCD1.DB7, LCM1602_IIC2.D7
  N23: LCD1.LED+, LCM1602_IIC2.A
  N24: LCD1.LED-, LCM1602_IIC2.K

notes:
  RFID:
  SCK = D5 #GPIO14
  MISO = D6 #GPIO12
  MOSI = D7 #GPIO13
  SDA = D8 #GPIO15
  RST = N/C
  IRQ = N/C
  Input Sensor: D3 #GPIO0
  Output Sensor: D4 #GPIO2
  Solenoid (Led): D0 #GPIO16
  LCD:
  SDA = D2 #GPIO4
  SCK = D1 #GPIO5
  5v
  3.3v

custom parts:
  NodeMCU V1.0: ESP8266 based NodeMCU
  RFID-RC522-v3: A simple China made RFID-RC522 Reader (6x4 cm); do check the pin labels, as this is a MFRC522 based clone.
  NeoPixel Stick: Make your own little LED strip arrangement with this stick of NeoPixel LEDs. We crammed 8 of the tiny 5050 (5mm x 5mm) smart RGB LEDs onto a PCB with mounting holes and a chainable design. Use only one microcontroller pin to control as many as you can chain together! Each LED is addressable as the driver chip is inside the LED. Each one has ~18mA constant current drive so the color will be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
  LCM1602 IIC: I2C-Module to use a 1602 or 2004 LCD on with the wire.h libory Serial LCD Modul
